# Fritzing sketch Schaltplan Makrolampe (saved by Fritzing 0.9.4)

parts:
  Nano = Arduino Nano (Rev3.0)
  Rotary_Encoder = Rotary Encoder [package=THT]
  BT1 = Pushbutton [package="[THT]"]
  Rotary_SW = Pushbutton [package="[THT]"]
  1W_LED = LED - 5mm [color="Blue (430nm)" package="5 mm [THT]"]
  1W_LED_2 = LED - 5mm [color="Blue (470nm)" package="5 mm [THT]"]
  R2 = Resistor [tolerance=±5% resistance=220 package=THT]
  BPT = NPN-Transistor [package="TO92 [THT]"]
  BPT_2 = NPN-Transistor [package="TO92 [THT]"]
  R1 = Resistor [tolerance=±5% resistance=220 package=THT]
  USB-C_Shutter = Power plug
  USB-Kable_+5V = Power plug

nets:
  GND: Nano.GND, Rotary_Encoder.EncoderPinC, BT1.Pin_1, BT1.Pin_2, Rotary_SW.Pin_1, Rotary_SW.Pin_2, 1W_LED.cathode, 1W_LED_2.cathode, USB-C_Shutter.GND, USB-Kable_+5V.GND
  N1: Nano.D4, USB-C_Shutter.VCC
  N2: Nano.D7, BT1.Pin_3, BT1.Pin_4
  N3: Nano.D9, R1.Pin_0
  N4: Nano.D10, R2.Pin_0
  N5: Nano.D12/MISO, Rotary_SW.Pin_3, Rotary_SW.Pin_4
  VIN: Nano.VIN, BPT.C, BPT_2.C, USB-Kable_+5V.VCC
  N6: Nano.A3, Rotary_Encoder.EncoderPinA
  N7: Nano.A2, Rotary_Encoder.EncoderPinB
  N8: 1W_LED.anode, BPT_2.E
  N9: 1W_LED_2.anode, BPT.E
  N10: R2.Pin_1, BPT_2.B
  N11: BPT.B, R1.Pin_1
